# Fritzing sketch Schematic2 (saved by Fritzing 0.9.3b)
breadboards: 1

parts:
  Pin_Mini_DIN_Female_Connector_Plug_for_PS2_interface1 = Arduino Uno (Rev3) - ICSP
  U2 = mini DIN 6 Connector [package=mini-din6]
  To_TFT_display1 = double row female pin header, 10 pins [form="♀ (female)"]
  R3 = Resistor [tolerance=±5% resistance=10k package=THT]
  R4 = Resistor [tolerance=±5% resistance=10k package=THT]

nets:
  N1: Pin_Mini_DIN_Female_Connector_Plug_for_PS2_interface1.A0, To_TFT_display1.pin1
  N2: Pin_Mini_DIN_Female_Connector_Plug_for_PS2_interface1.A1, To_TFT_display1.pin2
  N3: Pin_Mini_DIN_Female_Connector_Plug_for_PS2_interface1.A2, To_TFT_display1.pin3
  N4: Pin_Mini_DIN_Female_Connector_Plug_for_PS2_interface1.A3, To_TFT_display1.pin4
  N5: Pin_Mini_DIN_Female_Connector_Plug_for_PS2_interface1.A4/SDA, To_TFT_display1.pin5
  N6: Pin_Mini_DIN_Female_Connector_Plug_for_PS2_interface1.5V, U2.4, R3.Pin_1, R4.Pin_1
  N7: Pin_Mini_DIN_Female_Connector_Plug_for_PS2_interface1.D8, U2.1, R3.Pin_0
  N8: Pin_Mini_DIN_Female_Connector_Plug_for_PS2_interface1.GND, U2.2, U2.3
  N9: Pin_Mini_DIN_Female_Connector_Plug_for_PS2_interface1.D3_PWM, U2.5, U2.6, R4.Pin_0
