# Fritzing sketch schematics (saved by Fritzing 0.9.3b)
breadboards: 1

parts:
  U1 = mini DIN 6 Connector [package=mini-din6]
  Part1 = Arduino Uno (Rev3) - ICSP
  To_TFT_display = double row female pin header, 10 pins [form="♀ (female)"]
  R1 = Resistor [tolerance=±5% resistance=10k package=THT]
  R2 = Resistor [tolerance=±5% resistance=10k package=THT]

nets:
  N1: U1.1, Part1.D8, R1.Pin_0
  N2: U1.3, Part1.GND
  N3: U1.4, Part1.5V, R1.Pin_1, R2.Pin_1
  N4: U1.5, Part1.D3_PWM, R2.Pin_0
  N5: Part1.A0, To_TFT_display.pin1
  N6: Part1.A1, To_TFT_display.pin2
  N7: Part1.A2, To_TFT_display.pin3
  N8: Part1.A3, To_TFT_display.pin4
  N9: Part1.A4/SDA, To_TFT_display.pin5
